// Logisim project abrar.circ as structural Verilog: 5 circuits, main circuit main
module main (
);

  wire and_1_out, mips_alu_4_bit_1_p4, or_1_out, undriven, undriven_4, undriven_5, xor_1_out;
  wire [1:0] undriven_2;
  wire [3:0] demultiplexer_1_out1, demultiplexer_1_out1_3, mips_alu_4_bit_1_p3, mips_alu_4_bit_1_p5,
       multiplexer_1_out, registers_1_data_out_a, registers_1_data_out_b, rom_1_data;
  wire [7:0] adder_1_out, adder_2_out, multiplexer_2_out, register_1_q, undriven_3;
  wire [15:0] demultiplexer_1_out2, mips_alu_4_bit_1_p6;
  wire [15:4] demultiplexer_1_out1_2;
  wire [19:4] rom_1_data_2;

  Register register_1 (.D(multiplexer_2_out), .Q(register_1_q));  // open: en, clk, clr
  Adder adder_1 (.a(8'h1), .b(register_1_q), .out(adder_1_out));  // open: cin, cout
  ROM #(.dataWidth(20)) rom_1 (.addr(register_1_q), .data({rom_1_data_2, rom_1_data}));  // open: sel
  Registers registers_1 (
    .data_out_A(registers_1_data_out_a), .data_in(mips_alu_4_bit_1_p5), .regWrite(undriven),
    .addressA___R_W(demultiplexer_1_out1_3), .data_out_B(registers_1_data_out_b),
    .addressB__ReadOnly(demultiplexer_1_out1_2[15:12]));  // open: clock
  ROM #(.addrWidth(4), .dataWidth(4)) rom_2 ();  // open: addr, data, sel
  Multiplexer #(.width(4)) multiplexer_1 (
    .in0(registers_1_data_out_a), .in1(demultiplexer_1_out1), .out(multiplexer_1_out), .sel(undriven_2[0]));  // open: en
  // MIPS_ALU_4_bit mips_alu_4_bit_1: pin names not known; wires that end beside it: multiplexer_1_out, registers_1_data_out_b, mips_alu_4_bit_1_p3, mips_alu_4_bit_1_p4, mips_alu_4_bit_1_p5, mips_alu_4_bit_1_p6
  ROM #(.addrWidth(4), .dataWidth(4)) rom_3 (.addr(rom_1_data), .data(mips_alu_4_bit_1_p3));  // open: sel
  Demultiplexer #(.select(2), .width(16)) demultiplexer_1 (
    .out0(mips_alu_4_bit_1_p6),
    .out1({demultiplexer_1_out1_2[15:12], demultiplexer_1_out1_3, demultiplexer_1_out1_2[7:4], demultiplexer_1_out1}),
    .out2(demultiplexer_1_out2), .in(rom_1_data_2), .sel(undriven_2));  // open: out3, en
  Adder adder_2 (.a(adder_1_out), .b(undriven_3), .out(adder_2_out));  // open: cin, cout
  xor xor_1 (xor_1_out, mips_alu_4_bit_1_p4, undriven_4);
  or or_1 (or_1_out, xor_1_out, undriven_2[1]);
  Multiplexer #(.width(8)) multiplexer_2 (
    .in0(adder_1_out), .in1(adder_2_out), .out(multiplexer_2_out), .sel(and_1_out));  // open: en
  and and_1 (and_1_out, or_1_out, undriven_5);

  // Notes on the sheet:
  //   PC
  //   opcode
  //   contents of rom_2 (hex, n*v repeats v):
  //   f 6 6 2 6 2 2 2 1 8 9 6 c 0 1
  //   contents of rom_3 (hex, n*v repeats v):
  //   f 6 6 2 6 2 2 2 1 8 9 6 c 0 1
  //   branching
  //   i type
  //   j type
  //   jump
  //   src 2
  //   src 1
  //   JUMP TARGET ADDRESS
  //   jump magnitude
  //   IF BEQ then 0  if bneq then 1 
  //   jmp
  //   J TYPE?
  //   jmp/beq/bneq
endmodule

module ALU (
  input  [7:0] in_1,
  input  [7:0] in_2,
  input  [2:0] in_3,
  output [7:0] out_4
);

  wire [7:0] adder_1_out, and_1_out, nor_1_out, or_1_out, subtractor_1_out;

  Adder adder_1 (.a(in_1), .b(in_2), .out(adder_1_out));  // open: cin, cout
  Subtractor subtractor_1 (.a(in_1), .b(in_2), .out(subtractor_1_out));  // open: bin, bout
  assign and_1_out = in_1 & in_2;  // AND_Gate and_1, 8 bits wide
  assign or_1_out = in_1 | in_2;  // OR_Gate or_1, 8 bits wide
  assign nor_1_out = ~(in_1 | in_2);  // NOR_Gate nor_1, 8 bits wide
  Multiplexer #(.select(3), .width(8)) multiplexer_1 (
    .in0(adder_1_out), .in1(subtractor_1_out), .in2(and_1_out), .in3(or_1_out), .in4(nor_1_out), .out(out_4),
    .sel(in_3));  // open: in5, in6, in7, en
endmodule

module Registers (
  input  clock,
  input  [3:0] data_in,
  input  regWrite,
  input  [3:0] addressA___R_W,
  input  [3:0] addressB__ReadOnly,
  output [3:0] data_out_A,
  output [3:0] data_out_B
);

  wire demultiplexer_1_out0, demultiplexer_1_out1, demultiplexer_1_out2, demultiplexer_1_out3,
       demultiplexer_1_out4, demultiplexer_1_out14;
  wire [3:0] t0_q, t1_q, t2_q, t3_q, t4_q, ZERO_q;

  Demultiplexer #(.select(4)) demultiplexer_1 (
    .out0(demultiplexer_1_out0), .out1(demultiplexer_1_out1), .out2(demultiplexer_1_out2),
    .out3(demultiplexer_1_out3), .out4(demultiplexer_1_out4), .out14(demultiplexer_1_out14),
    .out15(demultiplexer_1_out14), .in(regWrite), .sel(addressA___R_W));  // open: out5, out6, out7, out8, out9, out10, out11, out12, out13, en
  Register #(.width(4)) t0 (.D(data_in), .en(demultiplexer_1_out0), .Q(t0_q), .clk(clock));  // open: clr
  Register #(.width(4)) t1 (.D(data_in), .en(demultiplexer_1_out1), .Q(t1_q), .clk(clock));  // open: clr
  Register #(.width(4)) t2 (.D(data_in), .en(demultiplexer_1_out3), .Q(t2_q), .clk(clock));  // open: clr
  Register #(.width(4)) t3 (.D(data_in), .en(demultiplexer_1_out2), .Q(t3_q), .clk(clock));  // open: clr
  Register #(.width(4)) t4 (.D(data_in), .en(demultiplexer_1_out4), .Q(t4_q), .clk(clock));  // open: clr
  Register #(.width(4)) ZERO (.D(4'b0000), .en(demultiplexer_1_out14), .Q(ZERO_q), .clk(clock));  // open: clr
  Multiplexer #(.select(4), .width(4), .enable("false")) multiplexer_1 (
    .in0(t0_q), .in1(t1_q), .in2(t2_q), .in3(t3_q), .in4(t4_q), .in15(ZERO_q), .out(data_out_A),
    .sel(addressA___R_W));  // open: in5, in6, in7, in8, in9, in10, in11, in12, in13, in14
  Multiplexer #(.select(4), .width(4)) multiplexer_2 (
    .in0(t0_q), .in1(t1_q), .in2(t2_q), .in3(t3_q), .in4(t4_q), .in15(ZERO_q), .out(data_out_B),
    .sel(addressB__ReadOnly));  // open: in5, in6, in7, in8, in9, in10, in11, in12, in13, in14, en
endmodule

module control (
  input  [3:0] in_1,
  output Shift,
  output RegDest,
  output Jump,
  output Branch,
  output MemRead,
  output MemToReg,
  output MemWrite,
  output ALUSrc,
  output RegWrite
);

  ROM #(.addrWidth(4), .dataWidth(9)) rom_1 (
    .addr(in_1), .data({RegWrite, ALUSrc, MemWrite, MemToReg, MemRead, Branch, Jump, RegDest, Shift}));  // open: sel

  // Notes on the sheet:
  //   contents of rom_1 (hex, n*v repeats v):
  //   40 20 3 3 81 81 1b 6 3 181 181 20 81 81 81 3
endmodule

module InstructionDecode (
  input  [19:0] in_1,
  output [3:0] shiftAmount,
  output [3:0] DstReg,
  output [7:0] Address_Imm,
  output [3:0] SrcReg2,
  output [3:0] SrcReg1,
  output [7:0] TargetJump,
  output [3:0] opCode
);


  assign Address_Imm = in_1[7:0];
  assign DstReg = in_1[7:4];
  assign opCode = in_1[19:16];
  assign shiftAmount = in_1[3:0];
  assign SrcReg1 = in_1[15:12];
  assign SrcReg2 = in_1[11:8];
  assign TargetJump = in_1[15:8];
endmodule
