// Logisim project main.circ as structural Verilog: 3 circuits, main circuit main
module main (
);

  wire mips_alu_1_p1, mips_alu_1_p3, mips_alu_1_p6, mips_alu_1_p7, undriven;
  wire [3:0] rom_2_data;
  wire [7:0] adder_1_out, mips_alu_1_p4, register_1_q;
  wire [19:0] rom_1_data;

  Register register_1 (.Q(register_1_q), .clk(undriven));  // open: D, en, clr
  Adder adder_1 (.a(8'h1), .b(register_1_q), .out(adder_1_out));  // open: cin, cout
  ROM #(.dataWidth(20)) rom_1 (.addr(register_1_q), .data(rom_1_data));  // open: sel
  ROM #(.addrWidth(4), .dataWidth(4)) rom_2 (.addr(rom_1_data[19:16]), .data(rom_2_data));  // open: sel
  // MIPS_ALU mips_alu_1: pin names not known; wires that end beside it: mips_alu_1_p1, mips_alu_1_p1, mips_alu_1_p3, mips_alu_1_p4, rom_2_data, mips_alu_1_p6, mips_alu_1_p7, mips_alu_1_p6, mips_alu_1_p7
  Adder adder_2 (.a(adder_1_out), .b(mips_alu_1_p4));  // open: out, cin, cout

  // Notes on the sheet:
  //   branching
endmodule

module ALU (
  input  [7:0] in_1,
  input  [7:0] in_2,
  input  [2:0] in_3,
  output [7:0] out_4
);

  wire [7:0] adder_1_out, and_1_out, nor_1_out, or_1_out, subtractor_1_out;

  Adder adder_1 (.a(in_1), .b(in_2), .out(adder_1_out));  // open: cin, cout
  Subtractor subtractor_1 (.a(in_1), .b(in_2), .out(subtractor_1_out));  // open: bin, bout
  assign and_1_out = in_1 & in_2;  // AND_Gate and_1, 8 bits wide
  assign or_1_out = in_1 | in_2;  // OR_Gate or_1, 8 bits wide
  assign nor_1_out = ~(in_1 | in_2);  // NOR_Gate nor_1, 8 bits wide
  Multiplexer #(.select(3), .width(8)) multiplexer_1 (
    .in0(adder_1_out), .in1(subtractor_1_out), .in2(and_1_out), .in3(or_1_out), .in4(nor_1_out), .out(out_4),
    .sel(in_3));  // open: in5, in6, in7, en
endmodule

module Registers (
  input  in_1,
  input  [3:0] data_in,
  input  [2:0] in_3,
  output [3:0] out_4
);

  wire demultiplexer_2_out0, demultiplexer_2_out1, demultiplexer_2_out2, demultiplexer_2_out3,
       demultiplexer_2_out4, demultiplexer_2_out7;
  wire [2:0] undriven;
  wire [3:0] demultiplexer_1_out0, demultiplexer_1_out1, demultiplexer_1_out2, demultiplexer_1_out3,
       demultiplexer_1_out4, demultiplexer_1_out7, t0_q, t1_q, t2_q, t3_q, t4_q, ZERO_q;

  Demultiplexer #(.select(3), .width(4)) demultiplexer_1 (
    .out0(demultiplexer_1_out0), .out1(demultiplexer_1_out1), .out2(demultiplexer_1_out2),
    .out3(demultiplexer_1_out3), .out4(demultiplexer_1_out4), .out7(demultiplexer_1_out7), .in(data_in),
    .sel(in_3));  // open: out5, out6, en
  Demultiplexer #(.select(3)) demultiplexer_2 (
    .out0(demultiplexer_2_out0), .out1(demultiplexer_2_out1), .out2(demultiplexer_2_out2),
    .out3(demultiplexer_2_out3), .out4(demultiplexer_2_out4), .out7(demultiplexer_2_out7), .in(1'b1),
    .sel(in_3));  // open: out5, out6, en
  Register #(.width(4)) t0 (.D(demultiplexer_1_out0), .en(demultiplexer_2_out0), .Q(t0_q), .clk(in_1));  // open: clr
  Register #(.width(4)) t1 (.D(demultiplexer_1_out1), .en(demultiplexer_2_out1), .Q(t1_q), .clk(in_1));  // open: clr
  Register #(.width(4)) t2 (.D(demultiplexer_1_out2), .en(demultiplexer_2_out2), .Q(t2_q), .clk(in_1));  // open: clr
  Register #(.width(4)) t3 (.D(demultiplexer_1_out3), .en(demultiplexer_2_out3), .Q(t3_q), .clk(in_1));  // open: clr
  Register #(.width(4)) t4 (.D(demultiplexer_1_out4), .en(demultiplexer_2_out4), .Q(t4_q), .clk(in_1));  // open: clr
  Register #(.width(4)) ZERO (
    .D(demultiplexer_1_out7), .en(demultiplexer_2_out7), .Q(ZERO_q), .clk(in_1));  // open: clr
  Multiplexer #(.select(3), .width(4)) multiplexer_1 (
    .in0(t0_q), .in1(t1_q), .in2(t2_q), .in3(t3_q), .in4(t4_q), .in5(ZERO_q), .out(out_4), .sel(undriven));  // open: in6, in7, en
endmodule
